# Fritzing sketch Initial Motor Circuit (saved by Fritzing 0.9.3b)

parts:
  BAT1 = BC9VPC [package=bc9vpc]
  Part1 = Arduino Mega ADK (Rev3)
  M1 = DC Motor
  S1 = H-Bridge with L298N

nets:
  N1: BAT1.V+, S1.12V
  GND: BAT1.V-, Part1.GND, S1.GND
  N2: Part1.D11_PWM, S1.5V
  N3: Part1.D2_PWM, S1.ENA
  N4: Part1.D47, S1.IN2
  N5: Part1.D49, S1.IN1
  N6: M1.pin_1, S1.M2-02
  N7: M1.pin_2, S1.M2-01

custom parts:
  H-Bridge with L298N: h-bridge
